# Fritzing sketch Sketch (saved by Fritzing 0.9.2b)
breadboards: 2

parts:
  Pro_Micro1 = Pro Micro
  ENCODER1 = Rotary Encoder with Knob
  LCM1602_IIC1 = LCM1602 IIC [part_number="LCM1602 IIC" chip_label="LCM1602 IIC" package="DIP (Dual Inline) [THT]"]
  LCD1_20x5 = LCD screen
  R2 = Resistor [tolerance=±5% resistance=10k package=THT]
  R3 = Resistor [tolerance=±5% resistance=10k package=THT]
  U2 = AUDIO-JACK2 [package=audio-jack]
  R7 = Resistor [tolerance=±5% resistance=10k package=THT]
  U5 = Optocoupler [package=THT]
  U6 = Optocoupler [package=THT]
  R8 = Resistor [tolerance=±5% resistance=1k package="1206 [SMD]"]
  R9 = Resistor [tolerance=±5% resistance=1k package="1206 [SMD]"]
  C1 = Ceramic Capacitor [capacitance=1µF package="0805 [SMD, multilayer]"]
  C2 = Ceramic Capacitor [capacitance=1µF package="0805 [SMD, multilayer]"]
  S1 = H-Bridge with L298N
  M1 = Stepper Motor - Bipolar

nets:
  N1: Pro_Micro1.TX1, R3.Pin_0
  N2: Pro_Micro1.RX0, R2.Pin_0
  N3: Pro_Micro1.D2, LCM1602_IIC1.SDA
  N4: Pro_Micro1.D3, LCM1602_IIC1.SCL
  N5: Pro_Micro1.D4, ENCODER1.no_name_yet#4
  N6: Pro_Micro1.D5, S1.ENA
  N7: Pro_Micro1.D6, S1.IN1
  N8: Pro_Micro1.D7, S1.IN2
  N9: Pro_Micro1.D8, S1.IN3
  N10: Pro_Micro1.D9, S1.IN4
  N11: Pro_Micro1.D10, S1.ENB
  N12: Pro_Micro1.D16/MOSI, R9.Pin_0
  N13: Pro_Micro1.D14/MISO, R8.Pin_0
  N14: ENCODER1.no_name_yet#1, R2.Pin_1
  N15: ENCODER1.no_name_yet#2, ENCODER1.no_name_yet#5, LCM1602_IIC1.GND, U5.Pin_2, U6.Pin_2, C1.1, C2.1
  N16: ENCODER1.no_name_yet#3, R3.Pin_1
  VSS: LCM1602_IIC1.VSS, LCD1_20x5.VSS
  VDD: LCM1602_IIC1.VDD, LCD1_20x5.VDD
  N17: LCM1602_IIC1.V0, LCD1_20x5.V0
  N18: LCM1602_IIC1.RS, LCD1_20x5.RS
  N19: LCM1602_IIC1.RW, LCD1_20x5.R/W
  N20: LCM1602_IIC1.E, LCD1_20x5.E
  N21: LCM1602_IIC1.D0, LCD1_20x5.DB0
  N22: LCM1602_IIC1.D1, LCD1_20x5.DB1
  N23: LCM1602_IIC1.D2, LCD1_20x5.DB2
  N24: LCM1602_IIC1.D3, LCD1_20x5.DB3
  N25: LCM1602_IIC1.D4, LCD1_20x5.DB4
  N26: LCM1602_IIC1.D5, LCD1_20x5.DB5
  N27: LCM1602_IIC1.D6, LCD1_20x5.DB6
  N28: LCM1602_IIC1.D7, LCD1_20x5.DB7
  N29: LCM1602_IIC1.A, LCD1_20x5.LED-
  N30: LCM1602_IIC1.K, LCD1_20x5.LED+
  N31: LCM1602_IIC1.VCC, R7.Pin_0
  N32: LCM1602_IIC1.LED_A, LCM1602_IIC1.LED_B
  N33: U2.RING, U5.Pin_6
  N34: U2.SLEEVE, U5.Pin_4, U6.Pin_4
  N35: U2.TIP, U6.Pin_5
  N36: U5.Pin_1, R8.Pin_1
  N37: U5.Pin_3, C2.0
  N38: U6.Pin_1, R9.Pin_1
  N39: U6.Pin_3, C1.0
  N40: S1.M1-01, M1.D
  N41: S1.M1-02, M1.B
  N42: S1.M2-01, M1.C
  N43: S1.M2-02, M1.A

notes:
  Camera Remote Controller
  Tip - Shutter
  Ring - Focus
  Sleeve - Camera Ground
  Turntable

custom parts:
  Pro Micro: The SparkFun Pro Micro is a complete USB-based microcontoller development system, in a very small footprint, capable of implementing many types of projects. All programming can be done via the USB port.
  Rotary Encoder with Knob: Rotary Encoder with 1/4" Shaft and Knob
  LCM1602 IIC: I2C-Module to use a 1602 or 2004 LCD on with the wire.h libory Serial LCD Modul
  LCD screen: A standard character display, usually with 2x16 characters. Comes in many colors.
  H-Bridge with L298N: h-bridge
